// Logisim project CPU.circ as structural Verilog: 1 circuit, main circuit main
module main (
  input  reset,
  output [31:0] out_2,
  output out_3,
  output [4:0] out_4,
  output [31:0] out_5,
  output out_6,
  output [4:0] out_7,
  output [31:0] out_8
);

  ROM #(.addrWidth(16), .dataWidth(32)) rom_1 ();  // open: addr, data, sel
  RAM #(.addrWidth(16), .dataWidth(32)) ram_1 ();  // open: addr, data, sel, clk, ld, clr

  assign out_2 = {32{1'b0}};
  assign out_3 = 1'b0;
  assign out_4 = {5{1'b0}};
  assign out_5 = {32{1'b0}};
  assign out_6 = 1'b0;
  assign out_7 = {5{1'b0}};
  assign out_8 = {32{1'b0}};
endmodule
