// Logisim project 4bit_swap.circ as structural Verilog: 4 circuits, main circuit 1bit_swap
module _1bit_swap (
  input  a,
  input  b,
  input  c,
  output A_2,
  output B_2
);

  wire and_1_out, and_2_out, and_3_out, and_4_out, not_1_out, not_2_out;

  not not_1 (not_1_out, c);
  not not_2 (not_2_out, c);
  and and_1 (and_1_out, b, c);
  and and_2 (and_2_out, a, not_1_out);
  and and_3 (and_3_out, b, not_2_out);
  and and_4 (and_4_out, a, c);
  or or_1 (A_2, and_1_out, and_2_out);
  or or_2 (B_2, and_3_out, and_4_out);
endmodule

module _4bit_swap (
  input  [3:0] in_1,
  input  [3:0] in_2,
  input  in_3,
  output [3:0] out_4,
  output [3:0] out_5
);

  _1bit_swap u_1bit_swap_1 (.a(in_1[0]), .b(in_2[0]), .c(in_3), .A_2(out_4[0]), .B_2(out_5[0]));
  _1bit_swap u_1bit_swap_2 (.a(in_1[1]), .b(in_2[1]), .c(in_3), .A_2(out_4[1]), .B_2(out_5[1]));
  _1bit_swap u_1bit_swap_3 (.a(in_1[2]), .b(in_2[2]), .c(in_3), .A_2(out_4[2]), .B_2(out_5[2]));
  _1bit_swap u_1bit_swap_4 (.a(in_1[3]), .b(in_2[3]), .c(in_3), .A_2(out_4[3]), .B_2(out_5[3]));
endmodule

module _2_comparator (
  input  [3:0] in_1,
  input  [3:0] in_2,
  output [3:0] out_3,
  output [3:0] out_4
);

  wire comparator_1_gt;

  Comparator #(.width(4), .mode("unsigned")) comparator_1 (.a(in_1), .b(in_2), .gt(comparator_1_gt));  // open: eq, lt
  _4bit_swap u_4bit_swap_1 (.in_1(in_1), .in_2(in_2), .in_3(comparator_1_gt), .out_4(out_3), .out_5(out_4));
endmodule

module _4bit_sort (
  input  [3:0] in_1,
  input  [3:0] in_2,
  input  [3:0] in_3,
  input  [3:0] in_4,
  output [3:0] out_5,
  output [3:0] out_6,
  output [3:0] out_7,
  output [3:0] out_8
);

  wire [3:0] n2_comparator_1_out_3, n2_comparator_1_out_4, n2_comparator_2_out_3, n2_comparator_2_out_4,
       n2_comparator_3_out_3, n2_comparator_3_out_4, n2_comparator_4_out_4, n2_comparator_5_out_4;

  _2_comparator u_2_comparator_1 (
    .in_1(in_1), .in_2(in_2), .out_3(n2_comparator_1_out_3), .out_4(n2_comparator_1_out_4));
  _2_comparator u_2_comparator_2 (
    .in_1(n2_comparator_1_out_3), .in_2(in_3), .out_3(n2_comparator_2_out_3), .out_4(n2_comparator_2_out_4));
  _2_comparator u_2_comparator_3 (
    .in_1(n2_comparator_1_out_4), .in_2(n2_comparator_2_out_4), .out_3(n2_comparator_3_out_3),
    .out_4(n2_comparator_3_out_4));
  _2_comparator u_2_comparator_4 (
    .in_1(n2_comparator_2_out_3), .in_2(in_4), .out_3(out_5), .out_4(n2_comparator_4_out_4));
  _2_comparator u_2_comparator_5 (
    .in_1(n2_comparator_3_out_3), .in_2(n2_comparator_4_out_4), .out_3(out_6), .out_4(n2_comparator_5_out_4));
  _2_comparator u_2_comparator_6 (
    .in_1(n2_comparator_3_out_4), .in_2(n2_comparator_5_out_4), .out_3(out_7), .out_4(out_8));
endmodule
