// Logisim project 896_22_22.8.8.circ as structural Verilog
module exchange (
  input  [1:0] in_1,
  input  in_2,
  output [1:0] out_3
);

  wire nand_1_out, nand_2_out, nand_3_out, nand_4_out, nand_5_out, nand_6_out, nand_7_out, nand_8_out,
       nand_9_out, nand_10_out, nand_11_out, nand_12_out, nand_13_out, nand_14_out;

  nand nand_1 (nand_1_out, in_1[0], in_1[0]);
  nand nand_2 (nand_2_out, in_1[1], in_1[1]);
  nand nand_3 (nand_3_out, in_1[0], in_1[0]);
  nand nand_4 (nand_4_out, in_1[1], in_1[1]);
  nand nand_5 (nand_5_out, in_1[0], in_1[0]);
  nand nand_6 (nand_6_out, in_2, in_2);
  nand nand_7 (nand_7_out, in_1[1], in_1[1]);
  nand nand_8 (nand_8_out, in_2, in_2);
  nand nand_9 (nand_9_out, nand_1_out, in_1[1]);
  nand nand_10 (nand_10_out, in_1[0], nand_2_out);
  nand nand_11 (nand_11_out, nand_3_out, nand_4_out, in_2);
  nand nand_12 (nand_12_out, nand_5_out, in_1[1], nand_6_out);
  nand nand_13 (nand_13_out, in_1[0], nand_7_out, nand_8_out);
  nand nand_14 (nand_14_out, in_1[0], in_1[1], in_2);
  nand nand_15 (out_3[0], nand_9_out, nand_10_out);
  nand nand_16 (out_3[1], nand_11_out, nand_12_out, nand_13_out, nand_14_out);
endmodule

module \output  (
  input  [1:0] in_1,
  input  in_2,
  output out_3,
  output out_4,
  output out_5,
  output out_6,
  output out_7
);

  wire and_1_out, and_2_out, and_3_out, and_4_out, and_5_out, and_6_out, and_7_out, and_8_out, not_1_out,
       not_2_out, not_3_out, not_4_out, not_5_out, not_6_out, not_7_out, not_8_out, not_9_out, not_10_out,
       not_11_out, not_12_out;

  not not_1 (not_1_out, in_1[0]);
  not not_2 (not_2_out, in_1[1]);
  not not_3 (not_3_out, in_2);
  not not_4 (not_4_out, in_2);
  not not_5 (not_5_out, in_1[0]);
  not not_6 (not_6_out, in_1[1]);
  not not_7 (not_7_out, in_1[0]);
  not not_8 (not_8_out, in_1[1]);
  not not_9 (not_9_out, in_1[0]);
  not not_10 (not_10_out, in_2);
  not not_11 (not_11_out, in_1[1]);
  not not_12 (not_12_out, in_2);
  and and_1 (and_1_out, not_1_out, not_2_out, not_3_out);
  and and_2 (and_2_out, in_1[0], in_1[1], not_4_out);
  and and_3 (and_3_out, not_5_out, in_2, not_6_out);
  and and_4 (and_4_out, in_1[0], in_1[1], in_2);
  and and_5 (and_5_out, not_7_out, in_1[1], in_2);
  and and_6 (and_6_out, in_1[0], not_8_out, in_2);
  and and_7 (and_7_out, not_9_out, in_1[1], not_10_out);
  and and_8 (and_8_out, in_1[0], not_11_out, not_12_out);
  or or_1 (out_4, and_1_out, and_2_out);
  or or_2 (out_5, and_3_out, and_4_out);
  or or_3 (out_6, and_5_out, and_6_out);
  or or_4 (out_7, and_7_out, and_8_out);

  assign out_3 = 1'b0;
endmodule

module mod5 (
  input  in_1,
  output out_2,
  output out_3,
  output out_4,
  output out_5,
  output out_6
);

  wire clock_1_out;
  wire [1:0] exchange_1_out_3, register_1_q;

  exchange exchange_1 (.in_1(register_1_q), .in_2(in_1), .out_3(exchange_1_out_3));
  Register #(.width(2)) register_1 (.D(exchange_1_out_3), .Q(register_1_q), .clk(clock_1_out));  // open: en, clr
  Clock clock_1 (.out(clock_1_out));
  \output  output_1 (
    .in_1(register_1_q), .in_2(in_1), .out_3(out_2), .out_4(out_3), .out_5(out_4), .out_6(out_5),
    .out_7(out_6));
endmodule
