// Logisim project P0_L0_CRC.circ as structural Verilog: 3 circuits, main circuit main
module main (
  input  [3:0] in_1,
  input  [3:0] in_2,
  output [2:0] out_3,
  output out_4
);

  wire [3:0] multiplexer_1_out, xor_1_out;

  Comparator #(.width(4), .mode("unsigned")) comparator_1 (.a(in_1), .b(4'b0111), .gt(out_4));  // open: eq, lt
  assign xor_1_out = in_1 ^ in_2;  // XOR_Gate xor_1, 4 bits wide
  Multiplexer #(.width(4), .enable("false")) multiplexer_1 (
    .in0(in_1), .in1(xor_1_out), .out(multiplexer_1_out), .sel(out_4));
  Bit_Extender #(.in_width(4), .out_width(3)) bit_extender_1 (.in(multiplexer_1_out), .out(out_3));
endmodule

module CRC (
  input  [7:0] in_1,
  input  [3:0] in_2,
  output [10:0] out_3
);

  wire [2:0] main_1_out_3, ope_1_out_4, ope_2_out_4, ope_4_out_4, ope_5_out_4, ope_6_out_4, ope_7_out_4;

  ope ope_1 (.in_1(ope_7_out_4), .in_2(1'b0), .in_3(in_2), .out_4(ope_1_out_4));  // open: out_5
  main main_1 (.in_1(in_1[7:4]), .in_2(in_2), .out_3(main_1_out_3));  // open: out_4
  ope ope_2 (.in_1(ope_1_out_4), .in_2(1'b0), .in_3(in_2), .out_4(ope_2_out_4));  // open: out_5
  ope ope_3 (.in_1(ope_2_out_4), .in_2(1'b0), .in_3(in_2), .out_4(out_3[2:0]));  // open: out_5
  ope ope_4 (.in_1(main_1_out_3), .in_2(in_1[3]), .in_3(in_2), .out_4(ope_4_out_4));  // open: out_5
  ope ope_5 (.in_1(ope_4_out_4), .in_2(in_1[2]), .in_3(in_2), .out_4(ope_5_out_4));  // open: out_5
  ope ope_6 (.in_1(ope_5_out_4), .in_2(in_1[1]), .in_3(in_2), .out_4(ope_6_out_4));  // open: out_5
  ope ope_7 (.in_1(ope_6_out_4), .in_2(in_1[0]), .in_3(in_2), .out_4(ope_7_out_4));  // open: out_5

  assign out_3[10:3] = in_1;
endmodule

module ope (
  input  [2:0] in_1,
  input  in_2,
  input  [3:0] in_3,
  output [2:0] out_4,
  output out_5
);

  main main_1 (.in_1({in_1, in_2}), .in_2(in_3), .out_3(out_4), .out_4(out_5));
endmodule
