// Logisim project P0_L0_FSM.circ as structural Verilog: 2 circuits, main circuit fsm
module fsm (
  input  in_1,
  input  [1:0] in_2,
  output out_3
);

  wire and_1_out, clock_1_out, register_1_q, register_2_q, register_3_q, \组合逻辑_1_b0 , \组合逻辑_1_b1 ;

  \组合逻辑  \u_组合逻辑_1  (
    .a1(register_2_q), .a0(register_3_q), .in1(in_2[1]), .in0(in_2[0]), .b1(\组合逻辑_1_b1 ), .b0(\组合逻辑_1_b0 ),
    .out(out_3));
  Register #(.width(1)) register_1 (.D(in_1), .Q(register_1_q), .clk(clock_1_out));  // open: en, clr
  Clock clock_1 (.out(clock_1_out));
  and and_1 (and_1_out, register_1_q, in_1);
  Register #(.width(1)) register_2 (.D(\组合逻辑_1_b1 ), .Q(register_2_q), .clk(clock_1_out), .clr(and_1_out));  // open: en
  Register #(.width(1)) register_3 (.D(\组合逻辑_1_b0 ), .Q(register_3_q), .clk(clock_1_out), .clr(and_1_out));  // open: en
endmodule

module \组合逻辑  (
  input  a1,
  input  a0,
  input  in1,
  input  in0,
  output b1,
  output b0,
  output out
);

  wire not_1_out, not_2_out, not_3_out;

  and and_1 (b1, a0, not_1_out);
  not not_1 (not_1_out, in0);
  not not_2 (not_2_out, in1);
  and and_2 (b0, not_2_out, in0);
  and and_3 (out, a1, not_3_out);
  not not_3 (not_3_out, in0);
endmodule
