// Logisim project P0_L1_ftoi.circ as structural Verilog: 1 circuit, main circuit ftoi
module ftoi (
  input  [15:0] in_1,
  output [31:0] out_2
);

  wire and_1_out, comparator_3_eq, comparator_4_eq, not_2_out, not_3_out, subtractor_1_bout;
  wire [1:0] comparator_1_eq;
  wire [4:0] subtractor_1_out;
  wire [31:0] adder_1_out, adder_3_out, bit_extender_1_out, buma, multiplexer_1_out, multiplexer_2_out,
       multiplexer_3_out, not_1_out, shifter_1_out, shifter_2_out, shifter_3_out;

  assign bit_extender_1_out = {{22{1'b0}}, in_1[9:0]};  // Bit_Extender bit_extender_1
  Subtractor #(.width(5)) subtractor_1 (
    .a(in_1[14:10]), .b(5'b01111), .out(subtractor_1_out), .bout(subtractor_1_bout));  // open: bin
  Comparator #(.width(5), .mode("unsigned")) comparator_1 (
    .a(in_1[14:10]), .b({5{1'b1}}), .eq(comparator_1_eq[0]));  // open: gt, lt
  Comparator #(.width(5), .mode("unsigned")) comparator_2 (
    .a(in_1[14:10]), .b({5{1'b0}}), .eq(comparator_1_eq[1]));  // open: gt, lt
  Adder #(.width(32)) adder_1 (.a(bit_extender_1_out), .b(32'h400), .out(adder_1_out));  // open: cin, cout
  Shifter #(.width(32)) shifter_1 (.in(adder_1_out), .\dist (subtractor_1_out), .out(shifter_1_out));
  Shifter #(.width(32)) shifter_2 (.in(shifter_3_out), .\dist (5'b01010), .out(shifter_2_out));
  Comparator #(.width(32), .mode("unsigned")) comparator_3 (
    .a(shifter_2_out), .b(shifter_1_out), .eq(comparator_3_eq));  // open: gt, lt
  assign not_1_out = ~adder_3_out;  // NOT_Gate not_1, 32 bits wide
  Shifter #(.width(32), .shift("lr")) shifter_3 (.in(shifter_1_out), .\dist (5'b01010), .out(shifter_3_out));
  Bit_Extender #(.in_width(1), .out_width(32)) bit_extender_2 (.in(not_2_out));  // open: out
  not not_2 (not_2_out, comparator_3_eq);
  Adder #(.width(32)) adder_2 (.a(not_1_out), .b(32'h1), .out(buma));  // open: cin, cout
  Comparator #(.width(10), .mode("unsigned")) comparator_4 (
    .a(in_1[9:0]), .b({10{1'b0}}), .eq(comparator_4_eq));  // open: gt, lt
  Multiplexer #(.width(32)) multiplexer_1 (
    .in0(shifter_3_out), .in1(buma), .out(multiplexer_1_out), .sel(in_1[15]));  // open: en
  Adder #(.width(32)) adder_3 (.a(shifter_3_out), .b({32{1'b0}}), .out(adder_3_out));  // open: cin, cout
  not not_3 (not_3_out, comparator_4_eq);
  and and_1 (and_1_out, not_3_out, in_1[15]);
  Multiplexer #(.width(32)) multiplexer_2 (
    .in0(multiplexer_1_out), .in1(multiplexer_3_out), .out(multiplexer_2_out), .sel(subtractor_1_bout));  // open: en
  Multiplexer #(.width(32), .enable("false")) multiplexer_3 (
    .in0({32{1'b0}}), .in1({32{1'b1}}), .out(multiplexer_3_out), .sel(and_1_out));
  Multiplexer #(.select(2), .width(32)) multiplexer_4 (
    .in0(multiplexer_2_out), .in1({32{1'b0}}), .in2(multiplexer_3_out), .out(out_2), .sel(comparator_1_eq));  // open: in3, en

  // Other names for the same wires on the sheet: signed = in_1[15]
endmodule
