// Logisim project P0_L1_navigation_2020.circ as structural Verilog: 3 circuits, main circuit navigation
module navigation (
  input  [1:0] in_1,
  input  in_2,
  input  in_3,
  output out_4,
  output out_5
);

  wire \组合逻辑2_1_out_4 ;
  wire [2:0] register_1_q, \组合逻辑2_1_out_3 ;

  \组合逻辑2  \u_组合逻辑2_1  (.in_1(in_1), .in_2(register_1_q), .out_3(\组合逻辑2_1_out_3 ), .out_4(\组合逻辑2_1_out_4 ));
  Register #(.width(3)) register_1 (.D(\组合逻辑2_1_out_3 ), .Q(register_1_q), .clk(in_2), .clr(in_3));  // open: en
  Register #(.width(1)) register_2 (.D(\组合逻辑2_1_out_4 ), .Q(out_5), .clk(in_2), .clr(in_3));  // open: en
  Comparator #(.width(3)) comparator_1 (.a(register_1_q), .b(3'b100), .eq(out_4));  // open: gt, lt
endmodule

module \组合逻辑  (
  input  dir1,
  input  dir0,
  input  a2,
  input  a1,
  input  a0,
  output b2,
  output b1,
  output b0,
  output hit
);

  wire and_1_out, and_2_out, and_3_out, and_4_out, and_5_out, and_6_out, and_7_out, and_8_out, and_9_out,
       and_10_out, and_11_out, and_12_out, and_13_out, and_14_out, and_15_out, and_16_out, not_1_out,
       not_2_out, not_3_out, not_4_out, not_5_out, not_6_out, not_7_out, not_8_out, not_9_out, not_10_out,
       not_11_out, not_12_out, not_13_out, not_14_out, not_15_out, not_16_out, not_17_out, not_18_out,
       not_19_out, not_20_out, not_21_out, not_22_out, not_23_out, not_24_out, not_25_out, not_26_out,
       not_27_out, not_28_out;

  not not_1 (not_1_out, dir1);
  not not_2 (not_2_out, dir0);
  not not_3 (not_3_out, a0);
  not not_4 (not_4_out, dir1);
  not not_5 (not_5_out, dir1);
  not not_6 (not_6_out, dir0);
  not not_7 (not_7_out, dir1);
  not not_8 (not_8_out, a1);
  not not_9 (not_9_out, dir1);
  not not_10 (not_10_out, a0);
  not not_11 (not_11_out, dir0);
  not not_12 (not_12_out, a0);
  not not_13 (not_13_out, dir1);
  not not_14 (not_14_out, dir0);
  not not_15 (not_15_out, a2);
  not not_16 (not_16_out, a1);
  not not_17 (not_17_out, dir0);
  not not_18 (not_18_out, dir1);
  not not_19 (not_19_out, dir0);
  not not_20 (not_20_out, dir1);
  not not_21 (not_21_out, a2);
  not not_22 (not_22_out, a0);
  not not_23 (not_23_out, a2);
  not not_24 (not_24_out, a1);
  not not_25 (not_25_out, a0);
  not not_26 (not_26_out, dir0);
  not not_27 (not_27_out, a2);
  not not_28 (not_28_out, a0);
  and and_1 (and_1_out, not_1_out, not_2_out, a1, not_3_out);
  and and_2 (and_2_out, not_4_out, dir0, a1, a0);
  and and_3 (and_3_out, not_5_out, not_6_out, a0);
  and and_4 (and_4_out, not_7_out, not_8_out, a0);
  and and_5 (and_5_out, not_9_out, dir0, a1, not_10_out);
  and and_6 (and_6_out, dir1, not_11_out, a1, not_12_out);
  and and_7 (and_7_out, dir1, dir0, a1, a0);
  and and_8 (and_8_out, not_13_out, not_14_out, not_15_out, not_16_out);
  and and_9 (and_9_out, not_17_out, a1, a0);
  and and_10 (and_10_out, dir1, dir0, a0);
  and and_11 (and_11_out, dir1, dir0, a1);
  and and_12 (and_12_out, not_18_out, not_19_out, a1, a0);
  and and_13 (and_13_out, not_20_out, dir0, not_21_out, not_22_out);
  and and_14 (and_14_out, dir0, not_23_out, not_24_out, not_25_out);
  and and_15 (and_15_out, dir1, not_26_out, not_27_out, not_28_out);
  and and_16 (and_16_out, dir1, dir0, a0);
  or or_1 (b2, and_1_out, and_2_out);
  or or_2 (b1, and_3_out, and_4_out, and_5_out, and_6_out, and_7_out);
  or or_3 (b0, and_8_out, and_9_out, and_10_out, and_11_out);
  or or_4 (hit, and_12_out, and_13_out, and_14_out, and_15_out, and_16_out);
endmodule

module \组合逻辑2  (
  input  [1:0] in_1,
  input  [2:0] in_2,
  output [2:0] out_3,
  output out_4
);

  \组合逻辑  \u_组合逻辑_1  (
    .dir1(in_1[1]), .dir0(in_1[0]), .a2(in_2[2]), .a1(in_2[1]), .a0(in_2[0]), .b2(out_3[2]), .b1(out_3[1]),
    .b0(out_3[0]), .hit(out_4));
endmodule
