// Logisim project fib_2.circ as structural Verilog: 7 circuits, main circuit 计算
module \计算  (
  input  [31:0] in_1,
  input  in_2,
  output [31:0] out_3,
  output [31:0] out_4,
  output [31:0] out_5,
  output [31:0] out_6
);

  wire \begin , clk, ok;
  wire [31:0] a00, a01, a10, a11, b00, b01, b10, b11, lst00, lst01, lst10, lst11, \矩阵乘法_1_out_9 ,
       \矩阵乘法_1_out_10 , \矩阵乘法_1_out_11 , \矩阵乘法_1_out_12 ;

  Multiplexer #(.width(32)) multiplexer_1 (.in0(32'h1), .in1(out_3), .out(lst00), .sel(\begin ));  // open: en
  Multiplexer #(.width(32)) multiplexer_2 (.in0({32{1'b0}}), .in1(out_4), .out(lst01), .sel(\begin ));  // open: en
  Multiplexer #(.width(32)) multiplexer_3 (.in0({32{1'b0}}), .in1(out_5), .out(lst10), .sel(\begin ));  // open: en
  Multiplexer #(.width(32)) multiplexer_4 (.in0(32'h1), .in1(out_6), .out(lst11), .sel(\begin ));  // open: en
  \最低位  \u_最低位_1  (.in_1(in_1), .in_2(in_2), .out_3(ok));
  Clock clock_1 (.out(clk));
  Counter #(.width(1), .max('h1), .ongoal("stay")) counter_1 (
    .Q(\begin ), .clk(clk), .clr(in_2));  // open: load, D, count, carry
  Multiplexer #(.width(32)) multiplexer_5 (.in0(32'h1), .in1(a00), .out(b00), .sel(ok));  // open: en
  Multiplexer #(.width(32)) multiplexer_6 (.in0({32{1'b0}}), .in1(a01), .out(b01), .sel(ok));  // open: en
  Multiplexer #(.width(32)) multiplexer_7 (.in0({32{1'b0}}), .in1(a10), .out(b10), .sel(ok));  // open: en
  Multiplexer #(.width(32)) multiplexer_8 (.in0(32'h1), .in1(a11), .out(b11), .sel(ok));  // open: en
  getA geta_1 (.in_1(in_2), .out_2(a00), .out_3(a01), .out_4(a10), .out_5(a11));
  \矩阵乘法  \u_矩阵乘法_1  (
    .in_1(lst00), .in_2(lst01), .in_3(lst10), .in_4(lst11), .in_5(b00), .in_6(b01), .in_7(b10), .in_8(b11),
    .out_9(\矩阵乘法_1_out_9 ), .out_10(\矩阵乘法_1_out_10 ), .out_11(\矩阵乘法_1_out_11 ), .out_12(\矩阵乘法_1_out_12 ));
  Register #(.width(32)) register_1 (.D(\矩阵乘法_1_out_9 ), .Q(out_3), .clk(clk));  // open: en, clr
  Register #(.width(32)) register_2 (.D(\矩阵乘法_1_out_10 ), .Q(out_4), .clk(clk));  // open: en, clr
  Register #(.width(32)) register_3 (.D(\矩阵乘法_1_out_11 ), .Q(out_5), .clk(clk));  // open: en, clr
  Register #(.width(32)) register_4 (.D(\矩阵乘法_1_out_12 ), .Q(out_6), .clk(clk));  // open: en, clr

  // Other names for the same wires on the sheet: ans00[31:0] = out_3; ans01[31:0] = out_4; ans10[31:0] = out_5;
  //   ans11[31:0] = out_6; reset = in_2
endmodule

module \矩阵乘法  (
  input  [31:0] in_1,
  input  [31:0] in_2,
  input  [31:0] in_3,
  input  [31:0] in_4,
  input  [31:0] in_5,
  input  [31:0] in_6,
  input  [31:0] in_7,
  input  [31:0] in_8,
  output [31:0] out_9,
  output [31:0] out_10,
  output [31:0] out_11,
  output [31:0] out_12
);

  \矩阵乘法组件  \u_矩阵乘法组件_1  (.in_1(in_1), .in_2(in_2), .in_3(in_5), .in_4(in_7), .out_5(out_9));
  \矩阵乘法组件  \u_矩阵乘法组件_2  (.in_1(in_1), .in_2(in_2), .in_3(in_6), .in_4(in_8), .out_5(out_10));
  \矩阵乘法组件  \u_矩阵乘法组件_3  (.in_1(in_3), .in_2(in_4), .in_3(in_5), .in_4(in_7), .out_5(out_11));
  \矩阵乘法组件  \u_矩阵乘法组件_4  (.in_1(in_3), .in_2(in_4), .in_3(in_6), .in_4(in_8), .out_5(out_12));

  // Other names for the same wires on the sheet: a00[31:0] = in_1; a01[31:0] = in_2; a10[31:0] = in_3;
  //   a11[31:0] = in_4; b00[31:0] = in_5; b01[31:0] = in_6; b10[31:0] = in_7; b11[31:0] = in_8
endmodule

module \矩阵乘法组件  (
  input  [31:0] in_1,
  input  [31:0] in_2,
  input  [31:0] in_3,
  input  [31:0] in_4,
  output [31:0] out_5
);

  wire [31:0] multiplier_1_out, multiplier_2_out;

  Multiplier #(.width(32)) multiplier_1 (.a(in_1), .b(in_3), .out(multiplier_1_out));  // open: cin, cout
  Multiplier #(.width(32)) multiplier_2 (.a(in_2), .b(in_4), .out(multiplier_2_out));  // open: cin, cout
  Adder #(.width(32)) adder_1 (.a(multiplier_1_out), .b(multiplier_2_out), .out(out_5));  // open: cin, cout
endmodule

module getA (
  input  in_1,
  output [31:0] out_2,
  output [31:0] out_3,
  output [31:0] out_4,
  output [31:0] out_5
);

  wire clk, ok;
  wire [31:0] last00, last01, last10, last11, \矩阵乘法_1_out_9 , \矩阵乘法_1_out_10 , \矩阵乘法_1_out_11 ,
       \矩阵乘法_1_out_12 ;

  Clock clock_1 (.out(clk));
  Counter #(.width(1), .max('h1), .ongoal("stay")) counter_1 (
    .Q(ok), .clk(clk), .clr(in_1));  // open: load, D, count, carry
  Multiplexer #(.width(32)) multiplexer_1 (.in0({32{1'b0}}), .in1(last00), .out(out_2), .sel(ok));  // open: en
  Multiplexer #(.width(32)) multiplexer_2 (.in0(32'h1), .in1(last01), .out(out_3), .sel(ok));  // open: en
  Multiplexer #(.width(32)) multiplexer_3 (.in0(32'h1), .in1(last10), .out(out_4), .sel(ok));  // open: en
  Multiplexer #(.width(32)) multiplexer_4 (.in0(32'h1), .in1(last11), .out(out_5), .sel(ok));  // open: en
  \矩阵乘法  \u_矩阵乘法_1  (
    .in_1(out_2), .in_2(out_3), .in_3(out_4), .in_4(out_5), .in_5(out_2), .in_6(out_3), .in_7(out_4),
    .in_8(out_5), .out_9(\矩阵乘法_1_out_9 ), .out_10(\矩阵乘法_1_out_10 ), .out_11(\矩阵乘法_1_out_11 ),
    .out_12(\矩阵乘法_1_out_12 ));
  Register #(.width(32)) register_1 (.D(\矩阵乘法_1_out_9 ), .Q(last00), .clk(clk));  // open: en, clr
  Register #(.width(32)) register_2 (.D(\矩阵乘法_1_out_10 ), .Q(last01), .clk(clk));  // open: en, clr
  Register #(.width(32)) register_3 (.D(\矩阵乘法_1_out_11 ), .Q(last10), .clk(clk));  // open: en, clr
  Register #(.width(32)) register_4 (.D(\矩阵乘法_1_out_12 ), .Q(last11), .clk(clk));  // open: en, clr

  // Other names for the same wires on the sheet: a00[31:0] = out_2; a01[31:0] = out_3; a10[31:0] = out_4;
  //   a11[31:0] = out_5; reset = in_1
endmodule

module \最低位  (
  input  [31:0] in_1,
  input  in_2,
  output out_3
);

  wire clk, counter_1_q;
  wire [31:0] lst, multiplexer_1_out, shifter_1_out;

  Clock clock_1 (.out(clk));
  Counter #(.width(1), .max('h1), .ongoal("stay")) counter_1 (
    .Q(counter_1_q), .clk(clk), .clr(in_2));  // open: load, D, count, carry
  Multiplexer #(.width(32)) multiplexer_1 (
    .in0(in_1), .in1(lst), .out(multiplexer_1_out), .sel(counter_1_q));  // open: en
  Shifter #(.width(32), .shift("lr")) shifter_1 (.in(multiplexer_1_out), .\dist (5'b00001), .out(shifter_1_out));
  Register #(.width(32)) register_1 (.D(shifter_1_out), .Q(lst), .clk(clk));  // open: en, clr
  // Probe on lst
  Bit_Extender #(.in_width(32), .out_width(1)) bit_extender_1 (.in(multiplexer_1_out), .out(out_3));
endmodule

module main (
  input  [31:0] in_1,
  output [31:0] out_2
);

  wire ok, reset;
  wire [31:0] \计算_1_out_4 ;

  \计算  \u_计算_1  (.in_1(in_1), .in_2(reset), .out_4(\计算_1_out_4 ));  // open: out_3, out_5, out_6
  \计时  \u_计时_1  (.in_1(reset), .out_2(ok));
  Multiplexer #(.width(32)) multiplexer_1 (.in0({32{1'b0}}), .in1(\计算_1_out_4 ), .out(out_2), .sel(ok));  // open: en
  Clock clock_1 ();  // open: out
endmodule

module \计时  (
  input  in_1,
  output out_2
);

  wire clock_1_out;
  wire [5:0] counter_1_q;

  Clock clock_1 (.out(clock_1_out));
  Counter #(.width(6), .max('h3f), .ongoal("stay")) counter_1 (
    .Q(counter_1_q), .clk(clock_1_out), .clr(in_1));  // open: load, D, count, carry
  Comparator #(.width(6), .mode("unsigned")) comparator_1 (.a(6'b100001), .b(counter_1_q), .lt(out_2));  // open: gt, eq
endmodule
