// Logisim project fibnacci.circ as structural Verilog: 3 circuits, main circuit main
module main (
  input  [2:0] in_1,
  input  in_2,
  output [3:0] out_3
);

  wire output_signal;
  wire [3:0] fib_now;

  \计数逻辑  \u_计数逻辑_1  (.in_1(in_1), .in_2(in_2), .out_3(output_signal));
  \计算逻辑  \u_计算逻辑_1  (.in_1(in_2), .in_2(output_signal), .out_3(fib_now));
  // Probe on fib_now
  Clock clock_1 ();  // open: out
  Multiplexer #(.width(4)) multiplexer_1 (.in0(4'b0000), .in1(fib_now), .out(out_3), .sel(output_signal));  // open: en

  // Other names for the same wires on the sheet: reset = in_2
endmodule

module \计数逻辑  (
  input  [2:0] in_1,
  input  in_2,
  output out_3
);

  wire clock_1_out;
  wire [3:0] bit_extender_1_out, counter_1_q;

  assign bit_extender_1_out = {{1{1'b0}}, in_1};  // Bit_Extender bit_extender_1
  Counter #(.width(4), .max('hf), .ongoal("stay")) counter_1 (
    .Q(counter_1_q), .clk(clock_1_out), .clr(in_2));  // open: load, D, count, carry
  Clock clock_1 (.out(clock_1_out));
  // Probe on counter_1_q
  Comparator #(.width(4), .mode("unsigned")) comparator_1 (
    .a(bit_extender_1_out), .b(counter_1_q), .lt(out_3));  // open: gt, eq
endmodule

module \计算逻辑  (
  input  in_1,
  input  in_2,
  output [3:0] out_3
);

  wire clock_1_out, counter_1_q, not_1_out;
  wire [3:0] adder_1_out, multiplexer_1_out, pre;

  Counter #(.width(1), .max('h1), .ongoal("stay")) counter_1 (
    .Q(counter_1_q), .clk(clock_1_out), .clr(in_1));  // open: load, D, count, carry
  not not_1 (not_1_out, in_2);
  Adder #(.width(4)) adder_1 (.a(out_3), .b(pre), .out(adder_1_out));  // open: cin, cout
  Multiplexer #(.width(4)) multiplexer_1 (
    .in0(4'b0001), .in1(out_3), .out(multiplexer_1_out), .sel(counter_1_q));  // open: en
  Clock clock_1 (.out(clock_1_out));
  Register #(.width(4)) register_1 (.D(multiplexer_1_out), .en(not_1_out), .Q(pre), .clk(clock_1_out), .clr(in_1));
  Register #(.width(4)) register_2 (.D(adder_1_out), .en(not_1_out), .Q(out_3), .clk(clock_1_out), .clr(in_1));

  // Other names for the same wires on the sheet: now[3:0] = out_3
endmodule
