// Logisim project finalmod5.circ as structural Verilog: 3 circuits, main circuit main
module main (
  input  [1:0] in_1,
  input  in_2,
  output [1:0] out_3
);


  assign out_3 = {in_1[0], in_2};
endmodule

module mod5 (
  input  in_1,
  output out_2,
  output out_3,
  output out_4,
  output out_5,
  output out_6
);

  wire clock_1_out;
  wire [1:0] main_1_out_3, register_1_q;

  main main_1 (.in_1(register_1_q), .in_2(in_1), .out_3(main_1_out_3));
  Register #(.width(2)) register_1 (.D(main_1_out_3), .Q(register_1_q), .clk(clock_1_out));  // open: en, clr
  Clock clock_1 (.out(clock_1_out));
  tores tores_1 (.in_1(main_1_out_3), .out_2(out_3), .out_3(out_4), .out_4(out_6), .out_5(out_5));

  assign out_2 = 1'b0;
endmodule

module tores (
  input  [1:0] in_1,
  output out_2,
  output out_3,
  output out_4,
  output out_5
);

  Demultiplexer #(.select(2), .enable("false")) demultiplexer_1 (
    .out0(out_2), .out1(out_3), .out2(out_4), .out3(out_5), .in(1'b1), .sel(in_1));
endmodule
