// Logisim project qshr型有限状态机.circ as structural Verilog: 2 circuits, main circuit navigation
module navigation (
  input  [1:0] in_1,
  input  in_2,
  input  in_3,
  output out_4,
  output out_5
);

  wire counter_1_q, decoder_1_out0, demultiplexer_1_out0, demultiplexer_1_out1, demultiplexer_1_out2,
       demultiplexer_1_out3, demultiplexer_2_out0, demultiplexer_2_out1, demultiplexer_2_out2,
       demultiplexer_2_out3, demultiplexer_3_out0, demultiplexer_3_out1, demultiplexer_3_out2,
       demultiplexer_3_out3, demultiplexer_4_out0, demultiplexer_4_out1, demultiplexer_4_out2,
       demultiplexer_4_out3, or_1_out, or_2_out, or_3_out, or_4_out, or_5_out, or_6_out, or_7_out,
       register_1_q, register_2_q, register_3_q, register_5_q;

  Decoder #(.enable("false")) decoder_1 (.out0(decoder_1_out0), .sel(counter_1_q));  // open: out1
  Counter #(.width(1), .max('h1), .ongoal("stay")) counter_1 (
    .Q(counter_1_q), .clk(in_2), .clr(in_3));  // open: load, D, count, carry
  Demultiplexer #(.select(2), .enable("false")) demultiplexer_1 (
    .out0(demultiplexer_1_out0), .out1(demultiplexer_1_out1), .out2(demultiplexer_1_out2),
    .out3(demultiplexer_1_out3), .in(register_1_q), .sel(in_1));
  Register #(.width(1)) register_1 (.D(or_1_out), .Q(register_1_q), .clk(in_2), .clr(in_3));  // open: en
  or or_1 (or_1_out, demultiplexer_1_out0, demultiplexer_1_out3, demultiplexer_2_out0);
  Demultiplexer #(.select(2), .enable("false")) demultiplexer_2 (
    .out0(demultiplexer_2_out0), .out1(demultiplexer_2_out1), .out2(demultiplexer_2_out2),
    .out3(demultiplexer_2_out3), .in(register_2_q), .sel(in_1));
  or or_2 (or_2_out, demultiplexer_1_out2, demultiplexer_2_out3, demultiplexer_4_out3, demultiplexer_3_out0);
  Register #(.width(1)) register_2 (.D(or_2_out), .Q(register_2_q), .clk(in_2), .clr(in_3));  // open: en
  Register #(.width(1)) register_3 (.D(or_3_out), .Q(register_3_q), .clk(in_2), .clr(in_3));  // open: en
  or or_3 (or_3_out, in_3, demultiplexer_2_out2, demultiplexer_3_out1, demultiplexer_3_out2, demultiplexer_3_out3, out_4);
  or or_4 (or_4_out, register_3_q, decoder_1_out0);
  Demultiplexer #(.select(2), .enable("false")) demultiplexer_3 (
    .out0(demultiplexer_3_out0), .out1(demultiplexer_3_out1), .out2(demultiplexer_3_out2),
    .out3(demultiplexer_3_out3), .in(or_4_out), .sel(in_1));
  Register #(.width(1)) register_4 (.D(or_5_out), .Q(out_4), .clk(in_2), .clr(in_3));  // open: en
  or or_5 (or_5_out, demultiplexer_1_out1, demultiplexer_4_out0);
  or or_6 (or_6_out, demultiplexer_2_out1, demultiplexer_4_out1, demultiplexer_4_out2);
  Register #(.width(1)) register_5 (.D(or_6_out), .Q(register_5_q), .clk(in_2), .clr(in_3));  // open: en
  Demultiplexer #(.select(2), .enable("false")) demultiplexer_4 (
    .out0(demultiplexer_4_out0), .out1(demultiplexer_4_out1), .out2(demultiplexer_4_out2),
    .out3(demultiplexer_4_out3), .in(register_5_q), .sel(in_1));
  or or_7 (or_7_out, demultiplexer_1_out3, demultiplexer_1_out0, demultiplexer_2_out3, demultiplexer_4_out1, demultiplexer_4_out2, demultiplexer_3_out1, demultiplexer_3_out2, demultiplexer_3_out3);
  Register #(.width(1)) register_6 (.D(or_7_out), .Q(out_5), .clk(in_2), .clr(in_3));  // open: en

  // Other names for the same wires on the sheet: clk = in_2; in[1:0] = in_1; reset = in_3
endmodule

module node (
  input  in_1,
  input  in_2,
  output out_3
);

  wire counter_1_q;

  Counter #(.width(1), .max('h1), .ongoal("stay")) counter_1 (
    .Q(counter_1_q), .clk(in_1), .clr(in_2));  // open: load, D, count, carry
  Decoder #(.tristate("true"), .enable("false")) decoder_1 (.out0(out_3), .sel(counter_1_q));  // open: out1
endmodule
