// Logisim project swap.circ as structural Verilog: 1 circuit, main circuit swap
module swap (
  input  in_1,
  input  in_2,
  input  in_3,
  output out_4,
  output out_5
);

  wire not_1_out;

  assign out_5 = not_1_out ? in_1 : 1'bz;  // Controlled_Buffer controlled_buffer_1
  assign out_4 = not_1_out ? in_2 : 1'bz;  // Controlled_Buffer controlled_buffer_2
  not not_1 (not_1_out, in_3);
  assign out_5 = in_3 ? in_2 : 1'bz;  // Controlled_Buffer controlled_buffer_3
  assign out_4 = in_3 ? in_1 : 1'bz;  // Controlled_Buffer controlled_buffer_4
endmodule
