// Logisim project 状态机.circ as structural Verilog: 2 circuits, main circuit mod5
module mod5 (
  input  in_1,
  output out_2,
  output out_3,
  output out_4,
  output out_5,
  output out_6
);

  wire clock_1_out, register_1_q, register_2_q, register_3_q, register_4_q;

  men men_1 (
    .s01(register_1_q), .s10(register_2_q), .s11(register_3_q), .s00(register_4_q), .nx(in_1), .t01(out_4),
    .t10(out_6), .t11(out_5), .t00(out_3));
  Clock clock_1 (.out(clock_1_out));
  Register #(.width(1)) register_1 (.D(out_4), .Q(register_1_q), .clk(clock_1_out));  // open: en, clr
  Register #(.width(1)) register_2 (.D(out_6), .Q(register_2_q), .clk(clock_1_out));  // open: en, clr
  Register #(.width(1)) register_3 (.D(out_5), .Q(register_3_q), .clk(clock_1_out));  // open: en, clr
  Register #(.width(1)) register_4 (.D(out_3), .Q(register_4_q), .clk(clock_1_out));  // open: en, clr

  assign out_2 = 1'b0;
endmodule

module men (
  input  s01,
  input  s10,
  input  s11,
  input  s00,
  input  nx,
  output t01,
  output t10,
  output t11,
  output t00
);

  wire not_1_out, not_2_out, not_3_out, not_4_out, not_5_out, not_6_out, not_7_out, not_8_out, not_9_out,
       not_10_out;

  not not_1 (not_1_out, s01);
  not not_2 (not_2_out, s11);
  not not_3 (not_3_out, s10);
  not not_4 (not_4_out, s00);
  not not_5 (not_5_out, nx);
  not not_6 (not_6_out, s10);
  not not_7 (not_7_out, s00);
  not not_8 (not_8_out, s01);
  not not_9 (not_9_out, s11);
  not not_10 (not_10_out, nx);
  and and_1 (t01, not_1_out, not_2_out, nx);
  and and_2 (t10, not_3_out, not_4_out, not_5_out);
  and and_3 (t11, not_6_out, not_7_out, nx);
  and and_4 (t00, not_8_out, not_9_out, not_10_out);
endmodule
