// Logisim project CPU - v2 - 副本.circ as structural Verilog: 10 circuits, main circuit main
module main (
  input  in_1,
  input  dsadsadwadwadwas,
  output [31:0] out_3,
  output out_4,
  output [4:0] out_5,
  output [31:0] out_6,
  output out_7,
  output [4:0] out_8,
  output [31:0] out_9
);

  wire add, beq, branch, clk, load, lui, lw, ori, sub, sw;
  wire [4:0] MemAddr;
  wire [31:0] adder_1_out, jump, MemOutData, MemWriData, multiplexer_1_out, PC_4, PC_q, rs_data, rt_data;

  Clock clock_1 (.out(clk));
  Multiplexer #(.width(32), .disabled(0)) multiplexer_1 (
    .in0({32{1'b0}}), .in1(jump), .out(multiplexer_1_out), .sel(branch));  // open: en
  Pull_Resistor pull_resistor_1 (.node(branch));
  Pull_Resistor pull_resistor_2 (.node(out_5));
  Adder #(.width(32)) adder_1 (.a(PC_4), .b(multiplexer_1_out), .out(adder_1_out));  // open: cin, cout
  GRF grf_1 (
    .clk(clk), .reset(in_1), .A1(out_3[25:21]), .A2(out_3[20:16]), .A3(out_5), .WD(out_6), .RD1(rs_data),
    .RD2(rt_data));
  add add_1 (.en(add), .rs_data(rs_data), .rt_data(rt_data), .rd(out_3[15:11]), .RegWriData(out_6), .RegWriAddr(out_5));
  lw lw_1 (
    .en(lw), .rs_data(rs_data), .imm(out_3[15:0]), .rt(out_3[20:16]), .MemAddr(MemAddr), .RegWriAddr(out_5),
    .load(load));
  sw sw_1 (
    .en(sw), .rs_data(rs_data), .imm(out_3[15:0]), .rt_data(rt_data), .MemAddr(MemAddr),
    .MemWriData(MemWriData), .store(out_7));
  Register #(.width(32)) PC (.D(adder_1_out), .Q(PC_q), .clk(clk), .clr(in_1));  // open: en
  Pull_Resistor pull_resistor_3 (.node(out_6));
  // Probe on PC_q[6:2]
  Adder #(.width(32)) adder_2 (.a(PC_q), .b(32'h4), .out(PC_4));  // open: cin, cout
  Pull_Resistor pull_resistor_4 (.node(out_7));
  sub sub_1 (.en(sub), .rs_data(rs_data), .rt_data(rt_data), .rd(out_3[15:11]), .RegWriData(out_6), .RegWriAddr(out_5));
  ori ori_1 (.en(ori), .rs_data(rs_data), .imm(out_3[15:0]), .rt(out_3[20:16]), .RegWriData(out_6), .RegWriAddr(out_5));
  lui lui_1 (.en(lui), .imm(out_3[15:0]), .rt(out_3[20:16]), .RegWriData(out_6), .RegWriAddr(out_5));
  ROM #(.addrWidth(5), .dataWidth(32)) rom_1 (.addr(PC_q[6:2]), .data(out_3));  // open: sel
  RAM #(.addrWidth(5), .dataWidth(32), .bus("separate")) ram_1 (
    .addr(MemAddr), .din(MemWriData), .data(MemOutData), .str(out_7), .clk(clk), .ld(load), .clr(in_1));  // open: sel
  Pull_Resistor pull_resistor_5 (.node(load));
  assign out_6 = load ? MemOutData : 32'bz;  // Controlled_Buffer controlled_buffer_1
  beq beq_1 (.en(beq), .rs_data(rs_data), .rt_data(rt_data), .imm(out_3[15:0]), .branch(branch), .jump(jump));
  Deop_er Deop_er (
    .op(out_3[31:26]), .func(out_3[5:0]), .add(add), .sub(sub), .ori(ori), .lui(lui), .beq(beq), .lw(lw),
    .sw(sw));  // open: out_4
  or or_1 (out_4, add, sub, ori, lui, lw, dsadsadwadwadwas);
  Multiplexer #(.width(5)) multiplexer_2 (.in0({5{1'b0}}), .in1(MemAddr), .out(out_8), .sel(out_7));  // open: en
  Multiplexer #(.width(32)) multiplexer_3 (.in0({32{1'b0}}), .in1(rt_data), .out(out_9), .sel(out_7));  // open: en

  // Other names for the same wires on the sheet: func[5:0] = out_3[5:0]; imm[15:0] = out_3[15:0]; Instr[31:0] = out_3;
  //   shamt[4:0] = out_3[10:6]; rd[4:0] = out_3[15:11]; rt[4:0] = out_3[20:16]; rs[4:0] = out_3[25:21];
  //   op[5:0] = out_3[31:26]; RegWriAddr[4:0] = out_5; RegWriData[31:0] = out_6; reset = in_1; store = out_7;
  //   WriEn = out_4

  // Notes on the sheet:
  //   contents of rom_1 (hex, n*v repeats v):
  //   35290004 354a0008 ac0a0004 8d290000
endmodule

module GRF (
  input  clk,
  input  reset,
  input  [4:0] A1,
  input  [4:0] A2,
  input  [4:0] A3,
  input  [31:0] WD,
  output [31:0] RD1,
  output [31:0] RD2
);

  wire A3_0, A3_1, A3_2, A3_3, A3_4, A3_5, A3_6, A3_7, A3_8, A3_9, A3_10, A3_11, A3_12, A3_13, A3_14, A3_15,
       A3_16, A3_17, A3_18, A3_19, A3_20, A3_21, A3_22, A3_23, A3_24, A3_25, A3_26, A3_27, A3_28, A3_29,
       A3_30, A3_31;
  wire [31:0] A1_0, A1_1, A1_2, A1_3, A1_4, A1_5, A1_6, A1_7, A1_8, A1_9, A1_10, A1_11, A1_12, A1_13, A1_14,
       A1_15, A1_16, A1_17, A1_18, A1_19, A1_20, A1_21, A1_22, A1_23, A1_24, A1_25, A1_26, A1_27, A1_28,
       A1_29, A1_30, A1_31;

  Clock clock_1 ();  // open: out
  Register #(.width(32)) _0 (.en(A3_0), .Q(A1_0), .clk(clk), .clr(reset));  // open: D
  Register #(.width(32)) _4 (.D(WD), .en(A3_4), .Q(A1_4), .clk(clk), .clr(reset));
  Register #(.width(32)) _8 (.D(WD), .en(A3_8), .Q(A1_8), .clk(clk), .clr(reset));
  Register #(.width(32)) _12 (.D(WD), .en(A3_12), .Q(A1_12), .clk(clk), .clr(reset));
  Register #(.width(32)) _16 (.D(WD), .en(A3_16), .Q(A1_16), .clk(clk), .clr(reset));
  Register #(.width(32)) _20 (.D(WD), .en(A3_20), .Q(A1_20), .clk(clk), .clr(reset));
  Register #(.width(32)) _24 (.D(WD), .en(A3_24), .Q(A1_24), .clk(clk), .clr(reset));
  Register #(.width(32)) _28 (.D(WD), .en(A3_28), .Q(A1_28), .clk(clk), .clr(reset));
  Register #(.width(32)) _1 (.D(WD), .en(A3_1), .Q(A1_1), .clk(clk), .clr(reset));
  Register #(.width(32)) _5 (.D(WD), .en(A3_5), .Q(A1_5), .clk(clk), .clr(reset));
  Register #(.width(32)) _9 (.D(WD), .en(A3_9), .Q(A1_9), .clk(clk), .clr(reset));
  Register #(.width(32)) _13 (.D(WD), .en(A3_13), .Q(A1_13), .clk(clk), .clr(reset));
  Register #(.width(32)) _17 (.D(WD), .en(A3_17), .Q(A1_17), .clk(clk), .clr(reset));
  Register #(.width(32)) _21 (.D(WD), .en(A3_21), .Q(A1_21), .clk(clk), .clr(reset));
  Register #(.width(32)) _25 (.D(WD), .en(A3_25), .Q(A1_25), .clk(clk), .clr(reset));
  Register #(.width(32)) _29 (.D(WD), .en(A3_29), .Q(A1_29), .clk(clk), .clr(reset));
  Register #(.width(32)) _2 (.D(WD), .en(A3_2), .Q(A1_2), .clk(clk), .clr(reset));
  Register #(.width(32)) _6 (.D(WD), .en(A3_6), .Q(A1_6), .clk(clk), .clr(reset));
  Register #(.width(32)) _10 (.D(WD), .en(A3_10), .Q(A1_10), .clk(clk), .clr(reset));
  Register #(.width(32)) _14 (.D(WD), .en(A3_14), .Q(A1_14), .clk(clk), .clr(reset));
  Register #(.width(32)) _18 (.D(WD), .en(A3_18), .Q(A1_18), .clk(clk), .clr(reset));
  Register #(.width(32)) _22 (.D(WD), .en(A3_22), .Q(A1_22), .clk(clk), .clr(reset));
  Register #(.width(32)) _26 (.D(WD), .en(A3_26), .Q(A1_26), .clk(clk), .clr(reset));
  Register #(.width(32)) _30 (.D(WD), .en(A3_30), .Q(A1_30), .clk(clk), .clr(reset));
  Register #(.width(32)) _3 (.D(WD), .en(A3_3), .Q(A1_3), .clk(clk), .clr(reset));
  Register #(.width(32)) _7 (.D(WD), .en(A3_7), .Q(A1_7), .clk(clk), .clr(reset));
  Register #(.width(32)) _11 (.D(WD), .en(A3_11), .Q(A1_11), .clk(clk), .clr(reset));
  Register #(.width(32)) _15 (.D(WD), .en(A3_15), .Q(A1_15), .clk(clk), .clr(reset));
  Register #(.width(32)) _19 (.D(WD), .en(A3_19), .Q(A1_19), .clk(clk), .clr(reset));
  Register #(.width(32)) _23 (.D(WD), .en(A3_23), .Q(A1_23), .clk(clk), .clr(reset));
  Register #(.width(32)) _27 (.D(WD), .en(A3_27), .Q(A1_27), .clk(clk), .clr(reset));
  Register #(.width(32)) _31 (.D(WD), .en(A3_31), .Q(A1_31), .clk(clk), .clr(reset));
  Demultiplexer #(.select(5)) demultiplexer_1 (
    .out0(A3_0), .out1(A3_1), .out2(A3_2), .out3(A3_3), .out4(A3_4), .out5(A3_5), .out6(A3_6), .out7(A3_7),
    .out8(A3_8), .out9(A3_9), .out10(A3_10), .out11(A3_11), .out12(A3_12), .out13(A3_13), .out14(A3_14),
    .out15(A3_15), .out16(A3_16), .out17(A3_17), .out18(A3_18), .out19(A3_19), .out20(A3_20), .out21(A3_21),
    .out22(A3_22), .out23(A3_23), .out24(A3_24), .out25(A3_25), .out26(A3_26), .out27(A3_27), .out28(A3_28),
    .out29(A3_29), .out30(A3_30), .out31(A3_31), .in(1'b1), .sel(A3));  // open: en
  Multiplexer #(.select(5), .width(32)) multiplexer_1 (
    .in0(A1_0), .in1(A1_1), .in2(A1_2), .in3(A1_3), .in4(A1_4), .in5(A1_5), .in6(A1_6), .in7(A1_7),
    .in8(A1_8), .in9(A1_9), .in10(A1_10), .in11(A1_11), .in12(A1_12), .in13(A1_13), .in14(A1_14),
    .in15(A1_15), .in16(A1_16), .in17(A1_17), .in18(A1_18), .in19(A1_19), .in20(A1_20), .in21(A1_21),
    .in22(A1_22), .in23(A1_23), .in24(A1_24), .in25(A1_25), .in26(A1_26), .in27(A1_27), .in28(A1_28),
    .in29(A1_29), .in30(A1_30), .in31(A1_31), .out(RD1), .sel(A1));  // open: en
  Multiplexer #(.select(5), .width(32)) multiplexer_2 (
    .in0(A1_0), .in1(A1_1), .in2(A1_2), .in3(A1_3), .in4(A1_4), .in5(A1_5), .in6(A1_6), .in7(A1_7),
    .in8(A1_8), .in9(A1_9), .in10(A1_10), .in11(A1_11), .in12(A1_12), .in13(A1_13), .in14(A1_14),
    .in15(A1_15), .in16(A1_16), .in17(A1_17), .in18(A1_18), .in19(A1_19), .in20(A1_20), .in21(A1_21),
    .in22(A1_22), .in23(A1_23), .in24(A1_24), .in25(A1_25), .in26(A1_26), .in27(A1_27), .in28(A1_28),
    .in29(A1_29), .in30(A1_30), .in31(A1_31), .out(RD2), .sel(A2));  // open: en

  // Other names for the same wires on the sheet: R = reset
endmodule

module Deop_er (
  input  [5:0] op,
  input  [5:0] func,
  output add,
  output out_4,
  output sub,
  output ori,
  output lui,
  output beq,
  output lw,
  output sw
);

  wire comparator_2_eq, comparator_3_eq, special;

  Comparator #(.width(6)) comparator_1 (.a(op), .b({6{1'b0}}), .eq(special));  // open: gt, lt
  Comparator #(.width(6), .mode("unsigned")) comparator_2 (
    .a(func), .b(6'b100000), .eq(comparator_2_eq));  // open: gt, lt
  Comparator #(.width(6), .mode("unsigned")) comparator_3 (
    .a(func), .b(6'b100010), .eq(comparator_3_eq));  // open: gt, lt
  Comparator #(.width(6), .mode("unsigned")) comparator_4 (.a(op), .b(6'b001101), .eq(ori));  // open: gt, lt
  Comparator #(.width(6), .mode("unsigned")) comparator_5 (.a(op), .b(6'b001111), .eq(lui));  // open: gt, lt
  Comparator #(.width(6), .mode("unsigned")) comparator_6 (.a(op), .b(6'b000100), .eq(beq));  // open: gt, lt
  Comparator #(.width(6), .mode("unsigned")) comparator_7 (.a(op), .b(6'b100011), .eq(lw));  // open: gt, lt
  Comparator #(.width(6), .mode("unsigned")) comparator_8 (.a(op), .b(6'b101011), .eq(sw));  // open: gt, lt
  and and_1 (add, comparator_2_eq, special);
  and and_2 (sub, comparator_3_eq, special);
endmodule

module add (
  input  en,
  input  [31:0] rs_data,
  input  [31:0] rt_data,
  input  [4:0] rd,
  output [31:0] RegWriData,
  output [4:0] RegWriAddr
);

  wire [31:0] adder_1_out;

  assign RegWriData = en ? adder_1_out : 32'bz;  // Controlled_Buffer controlled_buffer_1
  Adder #(.width(32)) adder_1 (.a(rs_data), .b(rt_data), .out(adder_1_out));  // open: cin, cout
  assign RegWriAddr = en ? rd : 5'bz;  // Controlled_Buffer controlled_buffer_2
endmodule

module sub (
  input  en,
  input  [31:0] rs_data,
  input  [31:0] rt_data,
  input  [4:0] rd,
  output [31:0] RegWriData,
  output [4:0] RegWriAddr
);

  wire [31:0] subtractor_1_out;

  assign RegWriData = en ? subtractor_1_out : 32'bz;  // Controlled_Buffer controlled_buffer_1
  Subtractor #(.width(32)) subtractor_1 (.a(rs_data), .b(rt_data), .out(subtractor_1_out));  // open: bin, bout
  assign RegWriAddr = en ? rd : 5'bz;  // Controlled_Buffer controlled_buffer_2
endmodule

module ori (
  input  en,
  input  [31:0] rs_data,
  input  [15:0] imm,
  input  [4:0] rt,
  output [31:0] RegWriData,
  output [4:0] RegWriAddr
);

  wire [31:0] bit_extender_1_out, or_1_out;

  assign bit_extender_1_out = {{16{1'b0}}, imm};  // Bit_Extender bit_extender_1
  assign or_1_out = rs_data | bit_extender_1_out;  // OR_Gate or_1, 32 bits wide
  assign RegWriData = en ? or_1_out : 32'bz;  // Controlled_Buffer controlled_buffer_1
  assign RegWriAddr = en ? rt : 5'bz;  // Controlled_Buffer controlled_buffer_2
endmodule

module lui (
  input  en,
  input  [15:0] imm,
  input  [4:0] rt,
  output [31:0] RegWriData,
  output [4:0] RegWriAddr
);

  wire [31:0] bit_extender_1_out, shifter_1_out;

  assign bit_extender_1_out = {{16{1'b0}}, imm};  // Bit_Extender bit_extender_1
  Shifter #(.width(32)) shifter_1 (.in(bit_extender_1_out), .\dist (5'b10000), .out(shifter_1_out));
  assign RegWriData = en ? shifter_1_out : 32'bz;  // Controlled_Buffer controlled_buffer_1
  assign RegWriAddr = en ? rt : 5'bz;  // Controlled_Buffer controlled_buffer_2
endmodule

module beq (
  input  en,
  input  [31:0] rs_data,
  input  [31:0] rt_data,
  input  [15:0] imm,
  output branch,
  output [31:0] jump
);

  wire comparator_1_eq;
  wire [31:0] bit_extender_1_out, shifter_1_out;

  assign bit_extender_1_out = {{16{imm[15]}}, imm};  // Bit_Extender bit_extender_1
  Shifter #(.width(32)) shifter_1 (.in(bit_extender_1_out), .\dist (5'b00010), .out(shifter_1_out));
  assign branch = en ? comparator_1_eq : 1'bz;  // Controlled_Buffer controlled_buffer_1
  Comparator #(.width(32), .mode("unsigned")) comparator_1 (
    .a(rs_data), .b(rt_data), .eq(comparator_1_eq));  // open: gt, lt
  assign jump = en ? shifter_1_out : 32'bz;  // Controlled_Buffer controlled_buffer_2
endmodule

module lw (
  input  en,
  input  [31:0] rs_data,
  input  [15:0] imm,
  input  [4:0] rt,
  output [4:0] MemAddr,
  output [4:0] RegWriAddr,
  output load
);

  wire [31:0] adder_1_out, bit_extender_1_out;

  assign bit_extender_1_out = {{16{imm[15]}}, imm};  // Bit_Extender bit_extender_1
  Adder #(.width(32)) adder_1 (.a(rs_data), .b(bit_extender_1_out), .out(adder_1_out));  // open: cin, cout
  assign RegWriAddr = en ? rt : 5'bz;  // Controlled_Buffer controlled_buffer_1
  assign MemAddr = en ? adder_1_out[6:2] : 5'bz;  // Controlled_Buffer controlled_buffer_2
  assign load = en ? en : 1'bz;  // Controlled_Buffer controlled_buffer_3
endmodule

module sw (
  input  en,
  input  [31:0] rs_data,
  input  [15:0] imm,
  input  [31:0] rt_data,
  output [4:0] MemAddr,
  output [31:0] MemWriData,
  output store
);

  wire [31:0] adder_1_out, bit_extender_1_out;

  assign bit_extender_1_out = {{16{imm[15]}}, imm};  // Bit_Extender bit_extender_1
  Adder #(.width(32)) adder_1 (.a(rs_data), .b(bit_extender_1_out), .out(adder_1_out));  // open: cin, cout
  assign MemAddr = en ? adder_1_out[6:2] : 5'bz;  // Controlled_Buffer controlled_buffer_1
  assign MemWriData = en ? rt_data : 32'bz;  // Controlled_Buffer controlled_buffer_2
  assign store = en ? en : 1'bz;  // Controlled_Buffer controlled_buffer_3
endmodule
