// Logisim project CPU.circ as structural Verilog: 12 circuits, main circuit main
module main (
  input  in_1,
  output [31:0] out_2,
  output out_3,
  output [4:0] out_4,
  output [31:0] out_5,
  output out_6,
  output [4:0] out_7,
  output [31:0] out_8
);

  wire clk, I_jump, I_WE, is_I, isA, isR, jump, load, R_jump, R_WE;
  wire [4:0] MemAddr;
  wire [31:0] a_mips_1_out_4, A_out, adder_1_out, I_out, multiplexer_1_out, or_1_out, PC_4, PC_q, R_out,
       ram_1_data, rs_data, rt_data;

  Clock clock_1 (.out(clk));
  Multiplexer #(.width(32), .disabled(0)) multiplexer_1 (
    .in0({32{1'b0}}), .in1(or_1_out), .out(multiplexer_1_out), .sel(jump));  // open: en
  assign or_1_out = R_out | I_out;  // OR_Gate or_1, 32 bits wide
  Comparator #(.width(6), .mode("unsigned")) comparator_1 (.a(out_2[31:26]), .b({6{1'b0}}), .eq(isR));  // open: gt, lt
  isA isa_1 (.op(out_2[31:26]), .isA(isA));
  nor nor_1 (is_I, isR, isA);
  or or_2 (out_3, R_WE, load, I_WE);
  or or_3 (jump, R_jump, I_jump);
  Adder #(.width(32)) adder_1 (.a(PC_4), .b(multiplexer_1_out), .out(adder_1_out));  // open: cin, cout
  Register #(.width(32)) PC (.D(adder_1_out), .Q(PC_q), .clk(clk), .clr(in_1));  // open: en
  R_mips R_mips (
    .is_R(isR), .func(out_2[5:0]), .in1(rs_data), .in2(rt_data), .R_out(R_out), .R_jump(R_jump), .R_WE(R_WE));
  I_mips I_mips (
    .is_I(is_I), .op(out_2[31:26]), .in1(rs_data), .in2(rt_data), .imm16(out_2[15:0]), .out_6(I_out),
    .I_jump(I_jump), .I_WE(I_WE));
  A_mips a_mips_1 (
    .op(out_2[31:26]), .in1(rs_data), .imm16(out_2[15:0]),
    .out_4({a_mips_1_out_4[31:7], MemAddr, a_mips_1_out_4[1:0]}), .load(load), .store(out_6));
  // Probe on PC_q[6:2]
  Adder #(.width(32)) adder_2 (.a(PC_q), .b(32'h4), .out(PC_4));  // open: cin, cout
  // Probe on MemAddr
  // Probe on rt_data
  Multiplexer #(.width(5)) multiplexer_2 (.in0(out_2[20:16]), .in1(out_2[15:11]), .out(out_4), .sel(isR));  // open: en
  assign out_5 = I_out | A_out | R_out;  // OR_Gate or_4, 32 bits wide
  ROM #(.addrWidth(5), .dataWidth(32)) rom_1 (.addr(PC_q[6:2]), .data(out_2));  // open: sel
  grf grf_1 (
    .clk(clk), .reset(in_1), .WE(out_3), .A1(out_2[25:21]), .A2(out_2[20:16]), .A3(out_4), .WD(out_5),
    .RD1(rs_data), .RD2(rt_data));
  RAM #(.addrWidth(5), .dataWidth(32), .bus("separate")) ram_1 (
    .addr(MemAddr), .din(rt_data), .data(ram_1_data), .str(out_6), .clk(clk), .ld(load), .clr(in_1));  // open: sel
  Multiplexer #(.width(32)) multiplexer_3 (.in0({32{1'b0}}), .in1(ram_1_data), .out(A_out), .sel(load));  // open: en
  Multiplexer #(.width(5)) multiplexer_4 (.in0({5{1'b0}}), .in1(MemAddr), .out(out_7), .sel(out_6));  // open: en
  Multiplexer #(.width(32)) multiplexer_5 (.in0({32{1'b0}}), .in1(rt_data), .out(out_8), .sel(out_6));  // open: en

  // Other names for the same wires on the sheet: func[5:0] = out_2[5:0]; imm16[15:0] = out_2[15:0];
  //   Instr[31:0] = out_2; shamt[4:0] = out_2[10:6]; rd[4:0] = out_2[15:11]; rt[4:0] = out_2[20:16];
  //   rs[4:0] = out_2[25:21]; op[5:0] = out_2[31:26]; RegAddr[4:0] = out_4; RegData[31:0] = out_5; reset = in_1;
  //   store = out_6; WE = out_3

  // Notes on the sheet:
  //   contents of rom_1 (hex, n*v repeats v):
  //   3c090001 ac090000 8c0a0000 14a5020 ac0a0004 1495822 ac0b0008 112a0001 11290001 35290008 ac09000c
  //   8c090000 ac090010 10e3000b 0 3c087777 3508ffff 80022 34001100 e65020 34080000 34090001 340a0001
  //   10a4020 1109fffe 1000ffff 10a4020 1109fffe 1000ffff
endmodule

// GRF
module grf (
  input  clk,
  input  reset,
  input  WE,
  input  [4:0] A1,
  input  [4:0] A2,
  input  [4:0] A3,
  input  [31:0] WD,
  output [31:0] RD1,
  output [31:0] RD2
);

  wire A3_0, A3_1, A3_2, A3_3, A3_4, A3_5, A3_6, A3_7, A3_8, A3_9, A3_10, A3_11, A3_12, A3_13, A3_14, A3_15,
       A3_16, A3_17, A3_18, A3_19, A3_20, A3_21, A3_22, A3_23, A3_24, A3_25, A3_26, A3_27, A3_28, A3_29,
       A3_30, A3_31;
  wire [31:0] A1_0, A1_1, A1_2, A1_3, A1_4, A1_5, A1_6, A1_7, A1_8, A1_9, A1_10, A1_11, A1_12, A1_13, A1_14,
       A1_15, A1_16, A1_17, A1_18, A1_19, A1_20, A1_21, A1_22, A1_23, A1_24, A1_25, A1_26, A1_27, A1_28,
       A1_29, A1_30, A1_31;

  Register #(.width(32)) _0 (.en(A3_0), .Q(A1_0), .clk(clk), .clr(reset));  // open: D
  Register #(.width(32)) _4 (.D(WD), .en(A3_4), .Q(A1_4), .clk(clk), .clr(reset));
  Register #(.width(32)) _8 (.D(WD), .en(A3_8), .Q(A1_8), .clk(clk), .clr(reset));
  Register #(.width(32)) _12 (.D(WD), .en(A3_12), .Q(A1_12), .clk(clk), .clr(reset));
  Register #(.width(32)) _16 (.D(WD), .en(A3_16), .Q(A1_16), .clk(clk), .clr(reset));
  Register #(.width(32)) _20 (.D(WD), .en(A3_20), .Q(A1_20), .clk(clk), .clr(reset));
  Register #(.width(32)) _24 (.D(WD), .en(A3_24), .Q(A1_24), .clk(clk), .clr(reset));
  Register #(.width(32)) _28 (.D(WD), .en(A3_28), .Q(A1_28), .clk(clk), .clr(reset));
  Register #(.width(32)) _1 (.D(WD), .en(A3_1), .Q(A1_1), .clk(clk), .clr(reset));
  Register #(.width(32)) _5 (.D(WD), .en(A3_5), .Q(A1_5), .clk(clk), .clr(reset));
  Register #(.width(32)) _9 (.D(WD), .en(A3_9), .Q(A1_9), .clk(clk), .clr(reset));
  Register #(.width(32)) _13 (.D(WD), .en(A3_13), .Q(A1_13), .clk(clk), .clr(reset));
  Register #(.width(32)) _17 (.D(WD), .en(A3_17), .Q(A1_17), .clk(clk), .clr(reset));
  Register #(.width(32)) _21 (.D(WD), .en(A3_21), .Q(A1_21), .clk(clk), .clr(reset));
  Register #(.width(32)) _25 (.D(WD), .en(A3_25), .Q(A1_25), .clk(clk), .clr(reset));
  Register #(.width(32)) _29 (.D(WD), .en(A3_29), .Q(A1_29), .clk(clk), .clr(reset));
  Register #(.width(32)) _2 (.D(WD), .en(A3_2), .Q(A1_2), .clk(clk), .clr(reset));
  Register #(.width(32)) _6 (.D(WD), .en(A3_6), .Q(A1_6), .clk(clk), .clr(reset));
  Register #(.width(32)) _10 (.D(WD), .en(A3_10), .Q(A1_10), .clk(clk), .clr(reset));
  Register #(.width(32)) _14 (.D(WD), .en(A3_14), .Q(A1_14), .clk(clk), .clr(reset));
  Register #(.width(32)) _18 (.D(WD), .en(A3_18), .Q(A1_18), .clk(clk), .clr(reset));
  Register #(.width(32)) _22 (.D(WD), .en(A3_22), .Q(A1_22), .clk(clk), .clr(reset));
  Register #(.width(32)) _26 (.D(WD), .en(A3_26), .Q(A1_26), .clk(clk), .clr(reset));
  Register #(.width(32)) _30 (.D(WD), .en(A3_30), .Q(A1_30), .clk(clk), .clr(reset));
  Register #(.width(32)) _3 (.D(WD), .en(A3_3), .Q(A1_3), .clk(clk), .clr(reset));
  Register #(.width(32)) _7 (.D(WD), .en(A3_7), .Q(A1_7), .clk(clk), .clr(reset));
  Register #(.width(32)) _11 (.D(WD), .en(A3_11), .Q(A1_11), .clk(clk), .clr(reset));
  Register #(.width(32)) _15 (.D(WD), .en(A3_15), .Q(A1_15), .clk(clk), .clr(reset));
  Register #(.width(32)) _19 (.D(WD), .en(A3_19), .Q(A1_19), .clk(clk), .clr(reset));
  Register #(.width(32)) _23 (.D(WD), .en(A3_23), .Q(A1_23), .clk(clk), .clr(reset));
  Register #(.width(32)) _27 (.D(WD), .en(A3_27), .Q(A1_27), .clk(clk), .clr(reset));
  Register #(.width(32)) _31 (.D(WD), .en(A3_31), .Q(A1_31), .clk(clk), .clr(reset));
  Demultiplexer #(.select(5)) demultiplexer_1 (
    .out0(A3_0), .out1(A3_1), .out2(A3_2), .out3(A3_3), .out4(A3_4), .out5(A3_5), .out6(A3_6), .out7(A3_7),
    .out8(A3_8), .out9(A3_9), .out10(A3_10), .out11(A3_11), .out12(A3_12), .out13(A3_13), .out14(A3_14),
    .out15(A3_15), .out16(A3_16), .out17(A3_17), .out18(A3_18), .out19(A3_19), .out20(A3_20), .out21(A3_21),
    .out22(A3_22), .out23(A3_23), .out24(A3_24), .out25(A3_25), .out26(A3_26), .out27(A3_27), .out28(A3_28),
    .out29(A3_29), .out30(A3_30), .out31(A3_31), .in(WE), .sel(A3));  // open: en
  Multiplexer #(.select(5), .width(32)) multiplexer_1 (
    .in0(A1_0), .in1(A1_1), .in2(A1_2), .in3(A1_3), .in4(A1_4), .in5(A1_5), .in6(A1_6), .in7(A1_7),
    .in8(A1_8), .in9(A1_9), .in10(A1_10), .in11(A1_11), .in12(A1_12), .in13(A1_13), .in14(A1_14),
    .in15(A1_15), .in16(A1_16), .in17(A1_17), .in18(A1_18), .in19(A1_19), .in20(A1_20), .in21(A1_21),
    .in22(A1_22), .in23(A1_23), .in24(A1_24), .in25(A1_25), .in26(A1_26), .in27(A1_27), .in28(A1_28),
    .in29(A1_29), .in30(A1_30), .in31(A1_31), .out(RD1), .sel(A1));  // open: en
  Multiplexer #(.select(5), .width(32)) multiplexer_2 (
    .in0(A1_0), .in1(A1_1), .in2(A1_2), .in3(A1_3), .in4(A1_4), .in5(A1_5), .in6(A1_6), .in7(A1_7),
    .in8(A1_8), .in9(A1_9), .in10(A1_10), .in11(A1_11), .in12(A1_12), .in13(A1_13), .in14(A1_14),
    .in15(A1_15), .in16(A1_16), .in17(A1_17), .in18(A1_18), .in19(A1_19), .in20(A1_20), .in21(A1_21),
    .in22(A1_22), .in23(A1_23), .in24(A1_24), .in25(A1_25), .in26(A1_26), .in27(A1_27), .in28(A1_28),
    .in29(A1_29), .in30(A1_30), .in31(A1_31), .out(RD2), .sel(A2));  // open: en

  // Other names for the same wires on the sheet: R = reset
endmodule

module R_mips (
  input  is_R,
  input  [5:0] func,
  input  [31:0] in1,
  input  [31:0] in2,
  output [31:0] R_out,
  output R_jump,
  output R_WE
);

  wire add_out_8, jump1, jump2, sub_out_8, WE1, WE2;
  wire [31:0] out1, out2;

  R_add add (
    .is_R(is_R), .func(func), .in1(in1), .in2(in2), .out_8(add_out_8), .R_out(out1), .R_jump(jump1),
    .R_WE(WE1));
  R_sub sub (
    .is_R(is_R), .func(func), .in1(in1), .in2(in2), .out_8(sub_out_8), .R_out(out2), .R_jump(jump2),
    .R_WE(WE2));
  assign R_out = out1 | out2;  // OR_Gate or_1, 32 bits wide
  or or_2 (R_jump, jump1, jump2);
  or or_3 (R_WE, WE1, WE2);
endmodule

module R_add (
  input  is_R,
  input  [5:0] func,
  input  [31:0] in1,
  input  [31:0] in2,
  output [31:0] R_out,
  output R_jump,
  output R_WE,
  output out_8
);

  wire comparator_1_eq;
  wire [31:0] adder_1_out;

  Transistor transistor_1 ();  // open: in, out, gate
  Comparator #(.width(6), .mode("unsigned")) comparator_1 (
    .a(func), .b(6'b100000), .eq(comparator_1_eq));  // open: gt, lt
  and and_1 (out_8, is_R, comparator_1_eq);
  Adder #(.width(32)) adder_1 (.a(in1), .b(in2), .out(adder_1_out));  // open: cin, cout
  Multiplexer #(.width(32)) multiplexer_1 (.in0({32{1'b0}}), .in1(adder_1_out), .out(R_out), .sel(out_8));  // open: en
  Multiplexer multiplexer_2 (.in0(1'b0), .in1(1'b0), .out(R_jump), .sel(out_8));  // open: en
  Multiplexer multiplexer_3 (.in0(1'b0), .in1(1'b1), .out(R_WE), .sel(out_8));  // open: en

  // Other names for the same wires on the sheet: en = out_8
endmodule

module R_sub (
  input  is_R,
  input  [5:0] func,
  input  [31:0] in1,
  input  [31:0] in2,
  output [31:0] R_out,
  output R_jump,
  output R_WE,
  output out_8
);

  wire comparator_1_eq;
  wire [31:0] subtractor_1_out;

  Transistor transistor_1 ();  // open: in, out, gate
  Comparator #(.width(6), .mode("unsigned")) comparator_1 (
    .a(func), .b(6'b100010), .eq(comparator_1_eq));  // open: gt, lt
  and and_1 (out_8, is_R, comparator_1_eq);
  Subtractor #(.width(32)) subtractor_1 (.a(in1), .b(in2), .out(subtractor_1_out));  // open: bin, bout
  Multiplexer #(.width(32)) multiplexer_1 (
    .in0({32{1'b0}}), .in1(subtractor_1_out), .out(R_out), .sel(out_8));  // open: en
  Multiplexer multiplexer_2 (.in0(1'b0), .in1(1'b0), .out(R_jump), .sel(out_8));  // open: en
  Multiplexer multiplexer_3 (.in0(1'b0), .in1(1'b1), .out(R_WE), .sel(out_8));  // open: en

  // Other names for the same wires on the sheet: en = out_8
endmodule

module I_mips (
  input  is_I,
  input  [5:0] op,
  input  [31:0] in1,
  input  [31:0] in2,
  input  [15:0] imm16,
  output [31:0] out_6,
  output I_jump,
  output I_WE
);

  wire beq_out_9, jump1, jump2, jump3, lui_out_9, ori_out_9, WE1, WE2, WE3;
  wire [31:0] out1, out2, out3;

  I_ori ori (
    .is_I(is_I), .op(op), .in1(in1), .in2(in2), .imm(imm16), .out_9(ori_out_9), .I_out(out1), .I_jump(jump1),
    .I_WE(WE1));
  I_lui lui (
    .is_I(is_I), .op(op), .in1(in1), .in2(in2), .imm(imm16), .out_9(lui_out_9), .I_out(out2), .I_jump(jump2),
    .I_WE(WE2));
  I_beq beq (
    .is_I(is_I), .op(op), .in1(in1), .in2(in2), .imm(imm16), .out_9(beq_out_9), .I_out(out3), .I_jump(jump3),
    .I_WE(WE3));
  assign out_6 = out1 | out2 | out3;  // OR_Gate or_1, 32 bits wide
  or or_2 (I_jump, jump1, jump2, jump3);
  or or_3 (I_WE, WE1, WE2, WE3);

  // Other names for the same wires on the sheet: imm[15:0] = imm16
endmodule

module I_ori (
  input  is_I,
  input  [5:0] op,
  input  [31:0] in1,
  input  [31:0] in2,
  input  [15:0] imm,
  output [31:0] I_out,
  output I_jump,
  output I_WE,
  output out_9
);

  wire comparator_1_eq;
  wire [31:0] bit_extender_1_out, or_1_out;

  Transistor transistor_1 ();  // open: in, out, gate
  Comparator #(.width(6), .mode("unsigned")) comparator_1 (
    .a(op), .b(6'b001101), .eq(comparator_1_eq));  // open: gt, lt
  assign bit_extender_1_out = {{16{1'b0}}, imm};  // Bit_Extender bit_extender_1
  and and_1 (out_9, is_I, comparator_1_eq);
  assign or_1_out = in1 | bit_extender_1_out;  // OR_Gate or_1, 32 bits wide
  Multiplexer #(.width(32)) multiplexer_1 (.in0({32{1'b0}}), .in1(or_1_out), .out(I_out), .sel(out_9));  // open: en
  Multiplexer multiplexer_2 (.in0(1'b0), .in1(1'b0), .out(I_jump), .sel(out_9));  // open: en
  Multiplexer multiplexer_3 (.in0(1'b0), .in1(1'b1), .out(I_WE), .sel(out_9));  // open: en

  // Other names for the same wires on the sheet: en = out_9
endmodule

module I_lui (
  input  is_I,
  input  [5:0] op,
  input  [31:0] in1,
  input  [31:0] in2,
  input  [15:0] imm,
  output [31:0] I_out,
  output I_jump,
  output I_WE,
  output out_9
);

  wire comparator_1_eq;
  wire [31:0] bit_extender_1_out, shifter_1_out;

  Transistor transistor_1 ();  // open: in, out, gate
  Comparator #(.width(6), .mode("unsigned")) comparator_1 (
    .a(op), .b(6'b001111), .eq(comparator_1_eq));  // open: gt, lt
  assign bit_extender_1_out = {{16{1'b0}}, imm};  // Bit_Extender bit_extender_1
  and and_1 (out_9, is_I, comparator_1_eq);
  Shifter #(.width(32)) shifter_1 (.in(bit_extender_1_out), .\dist (5'b10000), .out(shifter_1_out));
  Multiplexer #(.width(32)) multiplexer_1 (
    .in0({32{1'b0}}), .in1(shifter_1_out), .out(I_out), .sel(out_9));  // open: en
  Multiplexer multiplexer_2 (.in0(1'b0), .in1(1'b0), .out(I_jump), .sel(out_9));  // open: en
  Multiplexer multiplexer_3 (.in0(1'b0), .in1(1'b1), .out(I_WE), .sel(out_9));  // open: en

  // Other names for the same wires on the sheet: en = out_9
endmodule

module I_beq (
  input  is_I,
  input  [5:0] op,
  input  [31:0] in1,
  input  [31:0] in2,
  input  [15:0] imm,
  output [31:0] I_out,
  output I_jump,
  output I_WE,
  output out_9
);

  wire comparator_1_eq, comparator_2_eq;
  wire [31:0] bit_extender_1_out, shifter_1_out;

  Transistor transistor_1 ();  // open: in, out, gate
  Comparator #(.width(6), .mode("unsigned")) comparator_1 (
    .a(op), .b(6'b000100), .eq(comparator_1_eq));  // open: gt, lt
  assign bit_extender_1_out = {{16{1'b0}}, imm};  // Bit_Extender bit_extender_1
  and and_1 (out_9, is_I, comparator_1_eq);
  Comparator #(.width(32), .mode("unsigned")) comparator_2 (.a(in1), .b(in2), .eq(comparator_2_eq));  // open: gt, lt
  Shifter #(.width(32)) shifter_1 (.in(bit_extender_1_out), .\dist (5'b00010), .out(shifter_1_out));
  Multiplexer #(.width(32), .disabled(0)) multiplexer_1 (
    .in0({32{1'b0}}), .in1(shifter_1_out), .out(I_out), .sel(out_9));  // open: en
  Multiplexer multiplexer_2 (.in0(1'b0), .in1(comparator_2_eq), .out(I_jump), .sel(out_9));  // open: en
  Multiplexer multiplexer_3 (.in0(1'b0), .in1(1'b0), .out(I_WE), .sel(out_9));  // open: en

  // Other names for the same wires on the sheet: en = out_9
endmodule

module isA (
  input  [5:0] op,
  output isA
);

  wire comparator_1_eq, comparator_2_eq;

  Comparator #(.width(6), .mode("unsigned")) comparator_1 (
    .a(op), .b(6'b100011), .eq(comparator_1_eq));  // open: gt, lt
  Comparator #(.width(6), .mode("unsigned")) comparator_2 (
    .a(op), .b(6'b101011), .eq(comparator_2_eq));  // open: gt, lt
  or or_1 (isA, comparator_1_eq, comparator_2_eq);
endmodule

module A_mips (
  input  [5:0] op,
  input  [31:0] in1,
  input  [15:0] imm16,
  output [31:0] out_4,
  output load,
  output store
);

  wire [31:0] bit_extender_1_out;

  assign bit_extender_1_out = {{16{imm16[15]}}, imm16};  // Bit_Extender bit_extender_1
  Comparator #(.width(6), .mode("unsigned")) comparator_1 (.a(op), .b(6'b100011), .eq(load));  // open: gt, lt
  Comparator #(.width(6), .mode("unsigned")) comparator_2 (.a(op), .b(6'b101011), .eq(store));  // open: gt, lt
  Adder #(.width(32)) adder_1 (.a(in1), .b(bit_extender_1_out), .out(out_4));  // open: cin, cout
endmodule

module controller (
  input  [5:0] in_1,
  output out_2,
  output out_3,
  output out_4,
  output out_5,
  output out_6,
  output out_7,
  output out_8,
  output out_9
);

  wire add_out, beq_out, lui_out, lw_out, nop_out, not_1_out, not_2_out, not_3_out, not_4_out, not_5_out,
       not_6_out, ori_out, sub_out, sw_out;

  not not_1 (not_1_out, in_1[4]);
  not not_2 (not_2_out, in_1[5]);
  not not_3 (not_3_out, in_1[3]);
  not not_4 (not_4_out, in_1[1]);
  not not_5 (not_5_out, in_1[2]);
  not not_6 (not_6_out, in_1[0]);
  and add (add_out, in_1[5], not_1_out, not_3_out, not_5_out, not_4_out, not_6_out);
  and sub (sub_out, in_1[5], not_1_out, not_3_out, not_5_out, in_1[1], not_6_out);
  and ori (ori_out, not_2_out, not_1_out, in_1[3], in_1[2], not_4_out, in_1[0]);
  and lw (lw_out, in_1[5], not_1_out, not_3_out, not_5_out, in_1[1], in_1[0]);
  and sw (sw_out, in_1[5], not_1_out, in_1[3], not_5_out, in_1[1], in_1[0]);
  and beq (beq_out, not_2_out, not_1_out, not_3_out, in_1[2], not_4_out, not_6_out);
  and lui (lui_out, not_2_out, not_1_out, in_1[3], in_1[2], in_1[1], in_1[0]);
  and nop (nop_out, not_6_out, not_4_out, not_5_out, not_3_out, not_1_out, not_2_out);
  or RegDst (out_2, add_out, sub_out);
  or ALUSrc (out_3, ori_out, lw_out, sw_out, lui_out);
  or RegWrite (out_5, add_out, sub_out, lui_out, ori_out, lw_out);
  buf MemtoReg (out_4, lw_out);  // OR_Gate
  buf MemWrite (out_6, sw_out);  // OR_Gate
  buf nPC_sel (out_7, beq_out);  // OR_Gate
  or ALUctr0 (out_8, add_out, lui_out, lw_out, sw_out);
  or ALUctr1 (out_9, ori_out, lui_out);
endmodule
