// Logisim project P0_L0_GRF.circ as structural Verilog: 2 circuits, main circuit grf
module grf (
  input  clk,
  input  reset,
  input  WE,
  input  [4:0] A1,
  input  [4:0] A2,
  input  [4:0] A3,
  input  [31:0] WD,
  output [31:0] RD1,
  output [31:0] RD2
);

  wire A3_0, A3_1, A3_2, A3_3, A3_4, A3_5, A3_6, A3_7, A3_8, A3_9, A3_10, A3_11, A3_12, A3_13, A3_14, A3_15,
       A3_16, A3_17, A3_18, A3_19, A3_20, A3_21, A3_22, A3_23, A3_24, A3_25, A3_26, A3_27, A3_28, A3_29,
       A3_30, A3_31;
  wire [31:0] A1_0, A1_1, A1_2, A1_3, A1_4, A1_5, A1_6, A1_7, A1_8, A1_9, A1_10, A1_11, A1_12, A1_13, A1_14,
       A1_15, A1_16, A1_17, A1_18, A1_19, A1_20, A1_21, A1_22, A1_23, A1_24, A1_25, A1_26, A1_27, A1_28,
       A1_29, A1_30, A1_31;

  Register #(.width(32)) _0 (.en(A3_0), .Q(A1_0), .clk(clk), .clr(reset));  // open: D
  Register #(.width(32)) _4 (.D(WD), .en(A3_4), .Q(A1_4), .clk(clk), .clr(reset));
  Register #(.width(32)) _8 (.D(WD), .en(A3_8), .Q(A1_8), .clk(clk), .clr(reset));
  Register #(.width(32)) _12 (.D(WD), .en(A3_12), .Q(A1_12), .clk(clk), .clr(reset));
  Register #(.width(32)) _16 (.D(WD), .en(A3_16), .Q(A1_16), .clk(clk), .clr(reset));
  Register #(.width(32)) _20 (.D(WD), .en(A3_20), .Q(A1_20), .clk(clk), .clr(reset));
  Register #(.width(32)) _24 (.D(WD), .en(A3_24), .Q(A1_24), .clk(clk), .clr(reset));
  Register #(.width(32)) _28 (.D(WD), .en(A3_28), .Q(A1_28), .clk(clk), .clr(reset));
  Register #(.width(32)) _1 (.D(WD), .en(A3_1), .Q(A1_1), .clk(clk), .clr(reset));
  Register #(.width(32)) _5 (.D(WD), .en(A3_5), .Q(A1_5), .clk(clk), .clr(reset));
  Register #(.width(32)) _9 (.D(WD), .en(A3_9), .Q(A1_9), .clk(clk), .clr(reset));
  Register #(.width(32)) _13 (.D(WD), .en(A3_13), .Q(A1_13), .clk(clk), .clr(reset));
  Register #(.width(32)) _17 (.D(WD), .en(A3_17), .Q(A1_17), .clk(clk), .clr(reset));
  Register #(.width(32)) _21 (.D(WD), .en(A3_21), .Q(A1_21), .clk(clk), .clr(reset));
  Register #(.width(32)) _25 (.D(WD), .en(A3_25), .Q(A1_25), .clk(clk), .clr(reset));
  Register #(.width(32)) _29 (.D(WD), .en(A3_29), .Q(A1_29), .clk(clk), .clr(reset));
  Register #(.width(32)) _2 (.D(WD), .en(A3_2), .Q(A1_2), .clk(clk), .clr(reset));
  Register #(.width(32)) _6 (.D(WD), .en(A3_6), .Q(A1_6), .clk(clk), .clr(reset));
  Register #(.width(32)) _10 (.D(WD), .en(A3_10), .Q(A1_10), .clk(clk), .clr(reset));
  Register #(.width(32)) _14 (.D(WD), .en(A3_14), .Q(A1_14), .clk(clk), .clr(reset));
  Register #(.width(32)) _18 (.D(WD), .en(A3_18), .Q(A1_18), .clk(clk), .clr(reset));
  Register #(.width(32)) _22 (.D(WD), .en(A3_22), .Q(A1_22), .clk(clk), .clr(reset));
  Register #(.width(32)) _26 (.D(WD), .en(A3_26), .Q(A1_26), .clk(clk), .clr(reset));
  Register #(.width(32)) _30 (.D(WD), .en(A3_30), .Q(A1_30), .clk(clk), .clr(reset));
  Register #(.width(32)) _3 (.D(WD), .en(A3_3), .Q(A1_3), .clk(clk), .clr(reset));
  Register #(.width(32)) _7 (.D(WD), .en(A3_7), .Q(A1_7), .clk(clk), .clr(reset));
  Register #(.width(32)) _11 (.D(WD), .en(A3_11), .Q(A1_11), .clk(clk), .clr(reset));
  Register #(.width(32)) _15 (.D(WD), .en(A3_15), .Q(A1_15), .clk(clk), .clr(reset));
  Register #(.width(32)) _19 (.D(WD), .en(A3_19), .Q(A1_19), .clk(clk), .clr(reset));
  Register #(.width(32)) _23 (.D(WD), .en(A3_23), .Q(A1_23), .clk(clk), .clr(reset));
  Register #(.width(32)) _27 (.D(WD), .en(A3_27), .Q(A1_27), .clk(clk), .clr(reset));
  Register #(.width(32)) _31 (.D(WD), .en(A3_31), .Q(A1_31), .clk(clk), .clr(reset));
  Demultiplexer #(.select(5)) demultiplexer_1 (
    .out0(A3_0), .out1(A3_1), .out2(A3_2), .out3(A3_3), .out4(A3_4), .out5(A3_5), .out6(A3_6), .out7(A3_7),
    .out8(A3_8), .out9(A3_9), .out10(A3_10), .out11(A3_11), .out12(A3_12), .out13(A3_13), .out14(A3_14),
    .out15(A3_15), .out16(A3_16), .out17(A3_17), .out18(A3_18), .out19(A3_19), .out20(A3_20), .out21(A3_21),
    .out22(A3_22), .out23(A3_23), .out24(A3_24), .out25(A3_25), .out26(A3_26), .out27(A3_27), .out28(A3_28),
    .out29(A3_29), .out30(A3_30), .out31(A3_31), .in(WE), .sel(A3));  // open: en
  Multiplexer #(.select(5), .width(32)) multiplexer_1 (
    .in0(A1_0), .in1(A1_1), .in2(A1_2), .in3(A1_3), .in4(A1_4), .in5(A1_5), .in6(A1_6), .in7(A1_7),
    .in8(A1_8), .in9(A1_9), .in10(A1_10), .in11(A1_11), .in12(A1_12), .in13(A1_13), .in14(A1_14),
    .in15(A1_15), .in16(A1_16), .in17(A1_17), .in18(A1_18), .in19(A1_19), .in20(A1_20), .in21(A1_21),
    .in22(A1_22), .in23(A1_23), .in24(A1_24), .in25(A1_25), .in26(A1_26), .in27(A1_27), .in28(A1_28),
    .in29(A1_29), .in30(A1_30), .in31(A1_31), .out(RD1), .sel(A1));  // open: en
  Multiplexer #(.select(5), .width(32)) multiplexer_2 (
    .in0(A1_0), .in1(A1_1), .in2(A1_2), .in3(A1_3), .in4(A1_4), .in5(A1_5), .in6(A1_6), .in7(A1_7),
    .in8(A1_8), .in9(A1_9), .in10(A1_10), .in11(A1_11), .in12(A1_12), .in13(A1_13), .in14(A1_14),
    .in15(A1_15), .in16(A1_16), .in17(A1_17), .in18(A1_18), .in19(A1_19), .in20(A1_20), .in21(A1_21),
    .in22(A1_22), .in23(A1_23), .in24(A1_24), .in25(A1_25), .in26(A1_26), .in27(A1_27), .in28(A1_28),
    .in29(A1_29), .in30(A1_30), .in31(A1_31), .out(RD2), .sel(A2));  // open: en

  // Other names for the same wires on the sheet: R = reset
endmodule

module main (
  input  in_1,
  input  [4:0] in_2,
  input  [31:0] in_3,
  output [31:0] out_4
);

  wire clk;
  wire [31:0] adder_1_out, imm, multiplexer_1_out;

  Multiplexer #(.width(32), .disabled(0)) multiplexer_1 (
    .in0({32{1'b0}}), .in1(imm), .out(multiplexer_1_out), .sel(in_1), .en(in_1));
  Clock clock_1 (.out(clk));
  Adder #(.width(32)) adder_1 (.a(in_3), .b(multiplexer_1_out), .out(adder_1_out));  // open: cin, cout
  // Probe on adder_1_out[4:0]
  ROM #(.addrWidth(5), .dataWidth(32)) rom_1 (.addr(in_2), .data(out_4));  // open: sel

  // Other names for the same wires on the sheet: PC_4[31:0] = in_3; branch = in_1; branchok = in_1; reset = in_1

  // Notes on the sheet:
  //   contents of rom_1 (hex, n*v repeats v):
  //   efadaa35 aaa35555
endmodule
